// Logisim project Hazard_detection.circ as structural Verilog: 1 circuit, main circuit main
module main (
  input  ID_EX_MemRead,
  input  ID_EX_RegisterRt_0,
  input  ID_EX_RegisterRt_1,
  input  ID_EX_RegisterRt_2,
  input  ID_EX_RegisterRt_3,
  input  ID_EX_RegisterRt_4,
  input  IF_ID_RegisterRs_0,
  input  IF_ID_RegisterRs_1,
  input  IF_ID_RegisterRs_2,
  input  IF_ID_RegisterRs_3,
  input  IF_ID_RegisterRs_4,
  input  IF_ID_RegisterRt_0,
  input  IF_ID_RegisterRt_1,
  input  IF_ID_RegisterRt_2,
  input  IF_ID_RegisterRt_3,
  input  IF_ID_RegisterRt_4,
  output PCWrite,
  output IF_IDWrite,
  output ControlMuxSel
);

  wire and_1_out, and_3_out, not_1_out, not_2_out, not_3_out, not_4_out, not_5_out, not_6_out, not_7_out,
       not_8_out, not_9_out, not_10_out, not_11_out, not_12_out, not_13_out, not_14_out, not_15_out,
       not_16_out, or_1_out, xnor_1_out, xnor_2_out, xnor_3_out, xnor_4_out, xnor_5_out, xnor_6_out,
       xnor_7_out, xnor_8_out, xnor_9_out, xnor_10_out;

  not not_1 (not_1_out, ID_EX_MemRead);
  not not_2 (not_2_out, ID_EX_RegisterRt_0);
  not not_3 (not_3_out, ID_EX_RegisterRt_1);
  not not_4 (not_4_out, ID_EX_RegisterRt_2);
  not not_5 (not_5_out, ID_EX_RegisterRt_3);
  not not_6 (not_6_out, ID_EX_RegisterRt_4);
  not not_7 (not_7_out, IF_ID_RegisterRs_0);
  not not_8 (not_8_out, IF_ID_RegisterRs_1);
  not not_9 (not_9_out, IF_ID_RegisterRs_2);
  not not_10 (not_10_out, IF_ID_RegisterRs_3);
  not not_11 (not_11_out, IF_ID_RegisterRs_4);
  not not_12 (not_12_out, IF_ID_RegisterRt_0);
  not not_13 (not_13_out, IF_ID_RegisterRt_1);
  not not_14 (not_14_out, IF_ID_RegisterRt_2);
  not not_15 (not_15_out, IF_ID_RegisterRt_3);
  not not_16 (not_16_out, IF_ID_RegisterRt_4);
  xnor xnor_1 (xnor_1_out, ID_EX_RegisterRt_0, IF_ID_RegisterRs_0);
  xnor xnor_2 (xnor_2_out, ID_EX_RegisterRt_1, IF_ID_RegisterRs_1);
  xnor xnor_3 (xnor_3_out, ID_EX_RegisterRt_2, IF_ID_RegisterRs_2);
  and and_1 (and_1_out, xnor_1_out, xnor_2_out, xnor_3_out, xnor_4_out, xnor_5_out);
  xnor xnor_4 (xnor_4_out, ID_EX_RegisterRt_3, IF_ID_RegisterRs_3);
  xnor xnor_5 (xnor_5_out, ID_EX_RegisterRt_4, IF_ID_RegisterRs_4);
  xnor xnor_6 (xnor_6_out, ID_EX_RegisterRt_0, IF_ID_RegisterRt_0);
  or or_1 (or_1_out, and_1_out, and_3_out);
  and and_2 (ControlMuxSel, or_1_out, ID_EX_MemRead);
  xnor xnor_7 (xnor_7_out, ID_EX_RegisterRt_1, IF_ID_RegisterRt_1);
  xnor xnor_8 (xnor_8_out, ID_EX_RegisterRt_2, IF_ID_RegisterRt_2);
  and and_3 (and_3_out, xnor_6_out, xnor_7_out, xnor_8_out, xnor_9_out, xnor_10_out);
  xnor xnor_9 (xnor_9_out, ID_EX_RegisterRt_3, IF_ID_RegisterRt_3);
  xnor xnor_10 (xnor_10_out, ID_EX_RegisterRt_4, IF_ID_RegisterRt_4);
  not not_17 (PCWrite, ControlMuxSel);
  not not_18 (IF_IDWrite, ControlMuxSel);
endmodule
