// Logisim project alu_control_PLA.circ as structural Verilog: 1 circuit, main circuit main
module main (
  input  inst_0,
  input  inst_1,
  input  inst_2,
  input  inst_3,
  input  inst_4,
  input  inst_5,
  input  alu_op_0,
  input  alu_op_1,
  output sel_0,
  output sel_1,
  output sel_2
);

  wire add_out, addi_out, addu_out, and_out, br_out, not_1_out, not_2_out, not_3_out, not_4_out, not_5_out,
       not_6_out, not_7_out, not_8_out, or_out, sll_out, slt_out, sltu_out, sub_out, subu_out;

  not not_1 (not_1_out, inst_0);
  not not_2 (not_2_out, inst_1);
  not not_3 (not_3_out, inst_2);
  not not_4 (not_4_out, inst_3);
  not not_5 (not_5_out, inst_4);
  not not_6 (not_6_out, inst_5);
  not not_7 (not_7_out, alu_op_0);
  not not_8 (not_8_out, alu_op_1);
  and add (add_out, not_1_out, not_2_out, not_3_out, not_4_out, not_5_out, inst_5, not_7_out, alu_op_1);
  and addu (addu_out, inst_0, not_2_out, not_3_out, not_4_out, not_5_out, inst_5, not_7_out, alu_op_1);
  and sub (sub_out, not_1_out, inst_1, not_3_out, not_4_out, not_5_out, inst_5, not_7_out, alu_op_1);
  and subu (subu_out, inst_0, inst_1, not_3_out, not_4_out, not_5_out, inst_5, not_7_out, alu_op_1);
  and \and  (and_out, not_1_out, not_2_out, inst_2, not_4_out, not_5_out, inst_5, not_7_out, alu_op_1);
  and \or  (or_out, inst_0, not_2_out, inst_2, not_4_out, not_5_out, inst_5, not_7_out, alu_op_1);
  and sll (sll_out, not_1_out, not_2_out, not_3_out, not_4_out, not_5_out, not_6_out, not_7_out, alu_op_1);
  and slt (slt_out, not_1_out, inst_1, not_3_out, inst_3, not_5_out, inst_5, not_7_out, alu_op_1);
  and sltu (sltu_out, inst_0, inst_1, not_3_out, inst_3, not_5_out, inst_5, not_7_out, alu_op_1);
  and addi (addi_out, not_7_out, not_8_out);
  and br (br_out, alu_op_0, not_8_out);
  or or_2 (sel_0, or_out, sll_out, slt_out, sltu_out);
  or or_3 (sel_1, add_out, addi_out, sub_out, subu_out, br_out, slt_out, sltu_out);
  or or_4 (sel_2, addu_out, sub_out, subu_out, sll_out, br_out, sltu_out);
endmodule
